# Fritzing sketch global_schematics (saved by Fritzing 0.9.3b)
breadboards: 1

parts:
  Part1 = Arduino Uno (Rev3)
  Part2 = Arduino Uno (Rev3)
  Part3 = Arduino Uno (Rev3)
  Part4 = Arduino Uno (Rev3)
  Part5 = Arduino Uno (Rev3)
  Part6 = Arduino Uno (Rev3)
  J1 = Basic Servo  # not connected
  J2 = Basic Servo  # not connected
  J3 = Basic Servo  # not connected
  J4 = Basic Servo  # not connected
  J5 = Basic Servo  # not connected
  J6 = Basic Servo  # not connected
  J7 = Basic Servo  # not connected
  J8 = Basic Servo  # not connected
  J9 = Basic Servo  # not connected
  J10 = Basic Servo  # not connected
  J11 = Basic Servo  # not connected
  J12 = Basic Servo  # not connected
  J13 = Basic Servo  # not connected
  J14 = Basic Servo  # not connected
  J15 = Basic Servo  # not connected
  J16 = Basic Servo  # not connected
  J17 = Basic Servo  # not connected
  J18 = Basic Servo  # not connected
  J19 = Basic Servo  # not connected
  J20 = Basic Servo  # not connected
  J21 = Basic Servo  # not connected
  J22 = Basic Servo  # not connected
  J23 = Basic Servo  # not connected
  J24 = Basic Servo  # not connected
  J25 = Basic Servo  # not connected
  J26 = Basic Servo  # not connected
  J27 = Basic Servo  # not connected
  J28 = Basic Servo  # not connected
  J29 = Basic Servo  # not connected
  J30 = Basic Servo  # not connected
  J31 = Basic Servo  # not connected
  J32 = Basic Servo  # not connected
  J33 = Basic Servo  # not connected
  J34 = Basic Servo  # not connected
  J35 = Basic Servo  # not connected
  J36 = Basic Servo  # not connected
  J37 = Basic Servo  # not connected
  J38 = Basic Servo  # not connected
  J39 = Basic Servo  # not connected
  J40 = Basic Servo  # not connected
  J41 = Basic Servo  # not connected
  J42 = Basic Servo  # not connected
  J43 = Basic Servo  # not connected
  J44 = Basic Servo  # not connected
  J45 = Basic Servo  # not connected
  J46 = Basic Servo  # not connected
  J47 = Basic Servo  # not connected
  J48 = Basic Servo  # not connected
  Raspberry_Pi_1 = Raspberry Pi 3 [part_number=RPI-3-V1.2]
  U1 = TRANSCHIPTC5747 [package=camera_sfv24r-2st_2]  # not connected
  R1 = Resistor [tolerance=±5% resistance=100k package="0402 [SMD]"]
  R2 = Resistor [tolerance=±5% resistance=100k package="0402 [SMD]"]

nets:
  N1: Part1.A4/SDA, Part2.A4/SDA, Part3.A4/SDA, Part4.A4/SDA, Part5.A4/SDA, Part6.A4/SDA, Raspberry_Pi_1.GPIO2, R1.Pin_1
  N2: Part1.A5/SCL, Part2.A5/SCL, Part3.A5/SCL, Part4.A5/SCL, Part5.A5/SCL, Part6.A5/SCL, Raspberry_Pi_1.GPIO3, R2.Pin_1
  GND: Part1.GND, Part2.GND, Part3.GND, Part4.GND, Part5.GND, Part6.GND, Raspberry_Pi_1.GND
  N3: Raspberry_Pi_1.5V, R1.Pin_0, R2.Pin_0
